# Fritzing sketch Drawdio (saved by Fritzing 0.9.3b)
circuit board: 9.39312cm x 1.70775cm
breadboards: 1

parts:
  R7 = Resistor [tolerance=±5% resistance=10M package=THT]
  Q2 = PNP-Transistor [package="TO92 [THT]"]
  C6 = Electrolytic Capacitor [capacitance=100µF voltage=10V package="100 mil [THT, electrolytic]"]
  J4 = Piezo Speaker
  R9 = Resistor [tolerance=±5% resistance=10k package=THT]
  R8 = Resistor [tolerance=±5% resistance=10 package=THT]
  C7 = Ceramic Capacitor [capacitance=570pF package="100 mil [THT, multilayer]"]
  R5 = Resistor [tolerance=±5% resistance=270k package=THT]
  IC2 = IC, DIP package, 8 pins [chip_label=IC]
  BAT1 = Battery Holders [package=battery-aaa]
  C4 = Ceramic Capacitor [capacitance=0.1µF package="200 mil [THT, multilayer]"]
  J5 = female pin header, 2 pins [form="♀ (female)"]

nets:
  N1: R7.Pin_0, C7.0, R5.Pin_0, IC2.pin2, IC2.pin6
  N2: R7.Pin_1, J4.pin1, R8.Pin_1, C7.1, IC2.pin1, BAT1.-, C4.1
  N3: Q2.E, R9.Pin_0, IC2.pin4, IC2.pin8, BAT1.+
  N4: Q2.B, IC2.pin3
  N5: Q2.C, C6.+, R8.Pin_0
  N6: C6.-, J4.pin2
  N7: R9.Pin_1, IC2.pin7, J5.pin2
  N8: R5.Pin_1, J5.pin1
  N9: IC2.pin5, C4.0

notes:
  Drawdio
  Amal Al-Khulaifi
  Group
